// Logisim project alu_lab.circ as structural Verilog: 9 circuits, main circuit main
module main (
  input  [4:0] in_1,
  input  in_2,
  input  in_3,
  input  [31:0] in_4,
  input  in_5,
  output [31:0] out_6,
  output [31:0] out_7,
  output Overflow,
  output Zero_signal,
  output Underflow
);

  wire control_unit_1_regdest, main_control_unit_1_aluop0, main_control_unit_1_aluop1;
  wire [3:0] aluop_funct_alucontrol_1_c0;
  wire [4:0] multiplexer_1_out;
  wire [31:0] multiplexer_2_out, RF_readdata1, RF_readdata2;

  control_unit control_unit_1 (
    .opcode({6{1'b0}}), .regDest(control_unit_1_regdest));  // open: o0, o1, o4, o5, branch, memRead, memToReg, memWrite, ALUSrc, regWrite, ALUOp1, ALUOp0
  Multiplexer #(.width(5), .enable("false")) multiplexer_1 (
    .in0(in_1), .in1(5'b01000), .out(multiplexer_1_out), .sel(in_2));
  Multiplexer #(.width(32), .enable("false")) multiplexer_2 (
    .in0(in_4), .in1(out_7), .out(multiplexer_2_out), .sel(in_5));
  main_control_unit main_control_unit_1 (
    .opcode({6{1'b0}}), .aluop1(main_control_unit_1_aluop1), .aluop0(main_control_unit_1_aluop0));
  register_file RF (
    .WriteData(multiplexer_2_out), .ControlPort(control_unit_1_regdest), .regDest(multiplexer_1_out),
    .readReg1(5'b01001), .readReg2(5'b01010), .readData1(RF_readdata1), .readData2(RF_readdata2));
  ALU_32 alu_32_1 (
    .num1(RF_readdata1), .num2(RF_readdata2), .operation(aluop_funct_alucontrol_1_c0), .ALUresult(out_7),
    .zero_signal(Zero_signal), .overflow_bit(Overflow), .underflow_bit(Underflow));
  aluop_funct_alucontrol aluop_funct_alucontrol_1 (
    .aluop1(main_control_unit_1_aluop1), .aluop0(main_control_unit_1_aluop0), .funct_bits(6'b100000),
    .c3(aluop_funct_alucontrol_1_c0[3]), .c2(aluop_funct_alucontrol_1_c0[2]),
    .c1(aluop_funct_alucontrol_1_c0[1]), .c0(aluop_funct_alucontrol_1_c0[0]));

  assign out_6 = 32'h12a4020;

  // Notes on the sheet:
  //   32-bit instruction
  //   Control Unit
  //   opcode -> ALUOp generator
  //   ALUOp generated
  //   ALU Control
  //   ALU_32
  //   Result
  //   Enable for ALU multiplexer
endmodule

module ALU_32 (
  input  [31:0] num1,
  input  [31:0] num2,
  input  [3:0] operation,
  output [31:0] ALUresult,
  output zero_signal,
  output overflow_bit,
  output underflow_bit
);

  wire comparator_1_lt;
  wire [31:0] adder_1_out, AND_out, bit_extender_1_out, OR_out, subtractor_1_out;

  assign AND_out = num1 & num2;  // AND_Gate AND, 32 bits wide
  assign OR_out = num1 | num2;  // OR_Gate OR, 32 bits wide
  Adder #(.width(32)) adder_1 (.a(num1), .b(num2), .out(adder_1_out));  // open: cin, cout
  Subtractor #(.width(32)) subtractor_1 (.a(num1), .b(num2), .out(subtractor_1_out));  // open: bin, bout
  Comparator #(.width(32)) comparator_1 (.a(num1), .b(num2), .lt(comparator_1_lt));  // open: gt, eq
  assign bit_extender_1_out = {{31{1'b0}}, comparator_1_lt};  // Bit_Extender bit_extender_1
  Multiplexer #(.select(4), .width(32), .enable("false")) multiplexer_1 (
    .in0(AND_out), .in1(OR_out), .in2(adder_1_out), .in6(subtractor_1_out), .in7(bit_extender_1_out),
    .out(ALUresult), .sel(operation));  // open: in3, in4, in5, in8, in9, in10, in11, in12, in13, in14, in15
  overflow overflow_1 (.in_1(num1), .in_2(num2), .in_3(adder_1_out), .out_4(overflow_bit));
  underflow underflow_1 (.in_1(num1), .in_2(num2), .in_3(subtractor_1_out), .out_4(underflow_bit));
  Comparator #(.width(32)) comparator_2 (.a(num1), .b(num2), .eq(zero_signal));  // open: gt, lt

  // Notes on the sheet:
  //   First 32 bit number
  //   Second 32 bit number
  //   0000
  //   0001
  //   0010
  //   ADD
  //   0110
  //   SUB
  //   0111
  //   SLT
  //   Zero signal
endmodule

module main_control_unit (
  input  [5:0] opcode,
  output aluop1,
  output aluop0
);

  wire not_1_out, not_2_out;

  not not_1 (not_1_out, opcode[3]);
  not not_2 (not_2_out, opcode[1]);
  and and_1 (aluop1, not_1_out, not_2_out);

  assign aluop0 = opcode[3];
endmodule

module aluop_funct_alucontrol (
  input  aluop1,
  input  aluop0,
  input  [5:0] funct_bits,
  output c3,
  output c2,
  output c1,
  output c0
);

  wire and_2_out, and_3_out, not_1_out, not_2_out;

  and and_1 (c2, aluop1, funct_bits[1]);
  not not_1 (not_1_out, aluop1);
  not not_2 (not_2_out, funct_bits[2]);
  and and_2 (and_2_out, aluop1, funct_bits[0]);
  and and_3 (and_3_out, aluop1, funct_bits[3]);
  or or_1 (c1, not_1_out, not_2_out);
  or or_2 (c0, and_2_out, and_3_out);

  assign c3 = 1'b0;
endmodule

module overflow (
  input  [31:0] in_1,
  input  [31:0] in_2,
  input  [31:0] in_3,
  output out_4
);

  wire and_1_out, and_2_out, not_1_out, not_2_out, not_3_out;

  not not_1 (not_1_out, in_2[31]);
  not not_2 (not_2_out, in_3[31]);
  not not_3 (not_3_out, in_1[31]);
  and and_1 (and_1_out, in_1[31], in_2[31], not_2_out);
  and and_2 (and_2_out, not_3_out, not_1_out, in_3[31]);
  or or_1 (out_4, and_1_out, and_2_out);

  // Notes on the sheet:
  //   Overflow Detection
endmodule

module underflow (
  input  [31:0] in_1,
  input  [31:0] in_2,
  input  [31:0] in_3,
  output out_4
);

  wire xor_1_out, xor_2_out;

  xor xor_1 (xor_1_out, in_1[31], in_2[31]);
  xor xor_2 (xor_2_out, in_1[31], in_3[31]);
  and and_1 (out_4, xor_1_out, xor_2_out);

  // Notes on the sheet:
  //   Underflow detection
endmodule

module register_file (
  input  [31:0] WriteData,
  input  ControlPort,
  input  [4:0] regDest,
  input  [4:0] readReg1,
  input  [4:0] readReg2,
  output [31:0] readData1,
  output [31:0] readData2
);

  wire _0, _1, _2, _3, _4, _5, _6, _7, _8, _9, _10, _11, _12, _13, _14, _15, _16, _17, _18, _19, _20, _21,
       _22, _23, _24, _25, _26, _27, _28, _29, _30, _31, clock_1_out, clock_2_out, clock_3_out, clock_4_out,
       clock_5_out, clock_6_out, clock_7_out, clock_8_out, clock_9_out, clock_10_out, clock_11_out,
       clock_12_out, clock_13_out, clock_14_out, clock_15_out, clock_16_out, clock_17_out, clock_18_out,
       clock_19_out, clock_20_out, clock_21_out, clock_22_out, clock_23_out, clock_24_out, clock_25_out,
       clock_26_out, clock_27_out, clock_28_out, clock_29_out, clock_30_out, clock_31_out, clock_32_out;
  wire [31:0] _00, _01, _02, _03, _04, _05, _06, _07, _08, _09, _010, _011, _012, _013, _014, _015, _016,
       _017, _018, _019, _020, _021, _022, _023, _024, _025, _026, _027, _028, _029, _030, _031;

  Demultiplexer #(.select(5), .enable("false")) demultiplexer_1 (
    .out0(_0), .out1(_1), .out2(_2), .out3(_3), .out4(_4), .out5(_5), .out6(_6), .out7(_7), .out8(_8),
    .out9(_9), .out10(_10), .out11(_11), .out12(_12), .out13(_13), .out14(_14), .out15(_15), .out16(_16),
    .out17(_17), .out18(_18), .out19(_19), .out20(_20), .out21(_21), .out22(_22), .out23(_23), .out24(_24),
    .out25(_25), .out26(_26), .out27(_27), .out28(_28), .out29(_29), .out30(_30), .out31(_31),
    .in(ControlPort), .sel(regDest));
  Register #(.width(32)) register_1 (.D(WriteData), .en(_0), .Q(_00), .clk(clock_1_out));  // open: clr
  Clock clock_1 (.out(clock_1_out));
  Register #(.width(32)) register_2 (.D(WriteData), .en(_1), .Q(_01), .clk(clock_2_out));  // open: clr
  Clock clock_2 (.out(clock_2_out));
  Register #(.width(32)) u__2 (.D(WriteData), .en(_2), .Q(_02), .clk(clock_3_out));  // open: clr
  Clock clock_3 (.out(clock_3_out));
  Register #(.width(32)) register_3 (.D(WriteData), .en(_3), .Q(_03), .clk(clock_4_out));  // open: clr
  Clock clock_4 (.out(clock_4_out));
  Register #(.width(32)) register_4 (.D(WriteData), .en(_4), .Q(_04), .clk(clock_5_out));  // open: clr
  Clock clock_5 (.out(clock_5_out));
  Clock clock_6 (.out(clock_6_out));
  Clock clock_7 (.out(clock_7_out));
  Clock clock_8 (.out(clock_8_out));
  Clock clock_9 (.out(clock_9_out));
  Clock clock_10 (.out(clock_10_out));
  Clock clock_11 (.out(clock_11_out));
  Clock clock_12 (.out(clock_12_out));
  Clock clock_13 (.out(clock_13_out));
  Clock clock_14 (.out(clock_14_out));
  Clock clock_15 (.out(clock_15_out));
  Clock clock_16 (.out(clock_16_out));
  Clock clock_17 (.out(clock_17_out));
  Clock clock_18 (.out(clock_18_out));
  Clock clock_19 (.out(clock_19_out));
  Clock clock_20 (.out(clock_20_out));
  Clock clock_21 (.out(clock_21_out));
  Clock clock_22 (.out(clock_22_out));
  Clock clock_23 (.out(clock_23_out));
  Clock clock_24 (.out(clock_24_out));
  Clock clock_25 (.out(clock_25_out));
  Clock clock_26 (.out(clock_26_out));
  Clock clock_27 (.out(clock_27_out));
  Clock clock_28 (.out(clock_28_out));
  Clock clock_29 (.out(clock_29_out));
  Clock clock_30 (.out(clock_30_out));
  Clock clock_31 (.out(clock_31_out));
  Clock clock_32 (.out(clock_32_out));
  Register #(.width(32)) register_5 (.D(WriteData), .en(_5), .Q(_05), .clk(clock_6_out));  // open: clr
  Register #(.width(32)) register_6 (.D(WriteData), .en(_6), .Q(_06), .clk(clock_7_out));  // open: clr
  Register #(.width(32)) register_7 (.D(WriteData), .en(_7), .Q(_07), .clk(clock_8_out));  // open: clr
  Register #(.width(32)) u__8 (.D(WriteData), .en(_8), .Q(_08), .clk(clock_9_out));  // open: clr
  Register #(.width(32)) register_8 (.D(WriteData), .en(_9), .Q(_09), .clk(clock_10_out));  // open: clr
  Register #(.width(32)) register_9 (.D(WriteData), .en(_10), .Q(_010), .clk(clock_11_out));  // open: clr
  Register #(.width(32)) register_10 (.D(WriteData), .en(_11), .Q(_011), .clk(clock_12_out));  // open: clr
  Register #(.width(32)) register_11 (.D(WriteData), .en(_12), .Q(_012), .clk(clock_13_out));  // open: clr
  Register #(.width(32)) u__13 (.D(WriteData), .en(_13), .Q(_013), .clk(clock_14_out));  // open: clr
  Register #(.width(32)) register_12 (.D(WriteData), .en(_14), .Q(_014), .clk(clock_15_out));  // open: clr
  Register #(.width(32)) register_13 (.D(WriteData), .en(_15), .Q(_015), .clk(clock_16_out));  // open: clr
  Register #(.width(32)) register_14 (.D(WriteData), .en(_16), .Q(_016), .clk(clock_17_out));  // open: clr
  Register #(.width(32)) register_15 (.D(WriteData), .en(_17), .Q(_017), .clk(clock_18_out));  // open: clr
  Register #(.width(32)) u__18 (.D(WriteData), .en(_18), .Q(_018), .clk(clock_19_out));  // open: clr
  Register #(.width(32)) register_16 (.D(WriteData), .en(_19), .Q(_019), .clk(clock_20_out));  // open: clr
  Register #(.width(32)) register_17 (.D(WriteData), .en(_20), .Q(_020), .clk(clock_21_out));  // open: clr
  Register #(.width(32)) register_18 (.D(WriteData), .en(_21), .Q(_021), .clk(clock_22_out));  // open: clr
  Register #(.width(32)) register_19 (.D(WriteData), .en(_22), .Q(_022), .clk(clock_23_out));  // open: clr
  Register #(.width(32)) u__23 (.D(WriteData), .en(_23), .Q(_023), .clk(clock_24_out));  // open: clr
  Register #(.width(32)) register_20 (.D(WriteData), .en(_24), .Q(_024), .clk(clock_25_out));  // open: clr
  Register #(.width(32)) register_21 (.D(WriteData), .en(_25), .Q(_025), .clk(clock_26_out));  // open: clr
  Register #(.width(32)) register_22 (.D(WriteData), .en(_26), .Q(_026), .clk(clock_27_out));  // open: clr
  Register #(.width(32)) register_23 (.D(WriteData), .en(_27), .Q(_027), .clk(clock_28_out));  // open: clr
  Register #(.width(32)) u__28 (.D(WriteData), .en(_28), .Q(_028), .clk(clock_29_out));  // open: clr
  Register #(.width(32)) register_24 (.D(WriteData), .en(_29), .Q(_029), .clk(clock_30_out));  // open: clr
  Register #(.width(32)) register_25 (.D(WriteData), .en(_30), .Q(_030), .clk(clock_31_out));  // open: clr
  Register #(.width(32)) register_26 (.D(WriteData), .en(_31), .Q(_031), .clk(clock_32_out));  // open: clr
  Multiplexer #(.select(5), .width(32), .enable("false")) multiplexer_1 (
    .in0(_00), .in1(_01), .in2(_02), .in3(_03), .in4(_04), .in5(_05), .in6(_06), .in7(_07), .in8(_08),
    .in9(_09), .in10(_010), .in11(_011), .in12(_012), .in13(_013), .in14(_014), .in15(_015), .in16(_016),
    .in17(_017), .in18(_018), .in19(_019), .in20(_020), .in21(_021), .in22(_022), .in23(_023), .in24(_024),
    .in25(_025), .in26(_026), .in27(_027), .in28(_028), .in29(_029), .in30(_030), .in31(_031),
    .out(readData1), .sel(readReg1));
  Multiplexer #(.select(5), .width(32), .enable("false")) multiplexer_2 (
    .in0(_00), .in1(_01), .in2(_02), .in3(_03), .in4(_04), .in5(_05), .in6(_06), .in7(_07), .in8(_08),
    .in9(_09), .in10(_010), .in11(_011), .in12(_012), .in13(_013), .in14(_014), .in15(_015), .in16(_016),
    .in17(_017), .in18(_018), .in19(_019), .in20(_020), .in21(_021), .in22(_022), .in23(_023), .in24(_024),
    .in25(_025), .in26(_026), .in27(_027), .in28(_028), .in29(_029), .in30(_030), .in31(_031),
    .out(readData2), .sel(readReg2));

  // Notes on the sheet:
  //   register on which data has to be written
  //   write this data onto a register
  //   0
  //   1
  //   3
  //   4
  //   5
  //   6
  //   7
  //   9
  //   10
  //   11
  //   12
  //   14
  //   15
  //   16
  //   17
  //   19
  //   20
  //   21
  //   22
  //   24
  //   25
  //   26
  //   27
  //   29
  //   30
  //   31
  //   register from which data has to be read
  //   register from which data has to be read
  //   read data from selected register number
  //   read data from selected register number
endmodule

module control_unit (
  input  o0,
  input  o1,
  input  [5:0] opcode,
  input  o4,
  input  o5,
  output regDest,
  output branch,
  output memRead,
  output memToReg,
  output memWrite,
  output ALUSrc,
  output regWrite,
  output ALUOp1,
  output ALUOp0
);

  wire not_3_out, not_4_out;

  not not_1 (regDest, opcode[2]);
  or or_1 (ALUSrc, opcode[3], opcode[2]);
  not not_2 (regWrite, opcode[3]);
  not not_3 (not_3_out, opcode[2]);
  not not_4 (not_4_out, opcode[3]);
  and and_1 (ALUOp1, not_3_out, not_4_out);

  assign ALUOp0 = opcode[3];
  assign branch = opcode[3];
  assign memRead = 1'b0;
  assign memToReg = 1'b0;
  assign memWrite = 1'b0;
endmodule

module inst_mem (
  input  [31:0] in_1,
  output [31:0] out_2
);

  wire clock_1_out;

  Register #(.width(32)) register_1 (.D(in_1), .Q(out_2), .clk(clock_1_out));  // open: en, clr
  Clock clock_1 (.out(clock_1_out));
endmodule
