// Logisim project mips.circ as structural Verilog: 11 circuits, main circuit main
module main (
);

  wire alu_32_1_zero_signal, and_1_out, clock_1_out, control_unit_circuit_1_alusrc,
       control_unit_circuit_1_branch, control_unit_circuit_1_memread, control_unit_circuit_1_memtoreg,
       control_unit_circuit_1_memwrite, control_unit_circuit_1_regdest, control_unit_circuit_1_regwrite;
  wire [1:0] control_unit_circuit_1_aluop;
  wire [3:0] aluop_funct_alucontrol_1_alu_control;
  wire [4:0] multiplexer_1_out;
  wire [31:0] adder_1_out, adder_2_out, alu_32_1_aluresult, bit_extender_1_out,
       data_memory_1_data_read_from_memory, instruction_memory_1_instruction_itself, multiplexer_2_out,
       multiplexer_3_out, multiplexer_4_out, PC_q, register_file_1_readdata1, register_file_1_readdata2,
       shifter_1_out;

  Clock clock_1 (.out(clock_1_out));
  Register #(.width(32)) PC (.D(multiplexer_3_out), .Q(PC_q), .clk(clock_1_out));  // open: en, clr
  instruction_memory instruction_memory_1 (
    .address_of_instruction(PC_q), .instruction_itself(instruction_memory_1_instruction_itself));
  Adder #(.width(32)) adder_1 (.a(PC_q), .b(32'h4), .out(adder_1_out));  // open: cin, cout
  Multiplexer #(.width(5), .enable("false")) multiplexer_1 (
    .in0(instruction_memory_1_instruction_itself[20:16]),
    .in1(instruction_memory_1_instruction_itself[15:11]), .out(multiplexer_1_out),
    .sel(control_unit_circuit_1_regdest));
  control_unit_circuit control_unit_circuit_1 (
    .opcode(instruction_memory_1_instruction_itself[31:26]), .regDest(control_unit_circuit_1_regdest),
    .branch(control_unit_circuit_1_branch), .memRead(control_unit_circuit_1_memread),
    .memToReg(control_unit_circuit_1_memtoreg), .ALUOp(control_unit_circuit_1_aluop),
    .memWrite(control_unit_circuit_1_memwrite), .ALUSrc(control_unit_circuit_1_alusrc),
    .regWrite(control_unit_circuit_1_regwrite));  // open: jump
  register_file register_file_1 (
    .WriteData(multiplexer_4_out), .ControlPort(control_unit_circuit_1_regwrite),
    .regDest(multiplexer_1_out), .readReg1(instruction_memory_1_instruction_itself[25:21]),
    .readReg2(instruction_memory_1_instruction_itself[20:16]), .readData1(register_file_1_readdata1),
    .readData2(register_file_1_readdata2));
  assign bit_extender_1_out = {{16{instruction_memory_1_instruction_itself[15]}}, instruction_memory_1_instruction_itself[15:0]};  // Bit_Extender bit_extender_1
  Multiplexer #(.width(32), .enable("false")) multiplexer_2 (
    .in0(register_file_1_readdata2), .in1(bit_extender_1_out), .out(multiplexer_2_out),
    .sel(control_unit_circuit_1_alusrc));
  Shifter #(.width(32)) shifter_1 (.in(bit_extender_1_out), .\dist (5'b00010), .out(shifter_1_out));
  ALU_32 alu_32_1 (
    .num1(register_file_1_readdata1), .num2(multiplexer_2_out), .ALUresult(alu_32_1_aluresult),
    .zero_signal(alu_32_1_zero_signal), .operation(aluop_funct_alucontrol_1_alu_control));  // open: overflow_bit, underflow_bit
  aluop_funct_alucontrol aluop_funct_alucontrol_1 (
    .ALUOp(control_unit_circuit_1_aluop), .funct_bits(instruction_memory_1_instruction_itself[5:0]),
    .ALU_Control(aluop_funct_alucontrol_1_alu_control));
  data_memory data_memory_1 (
    .memory_address(alu_32_1_aluresult), .data_to_be_written(register_file_1_readdata2),
    .data_read_from_memory(data_memory_1_data_read_from_memory), .in_3(control_unit_circuit_1_memread),
    .in_2(control_unit_circuit_1_memwrite));
  Multiplexer #(.width(32), .enable("false")) multiplexer_3 (
    .in0(adder_1_out), .in1(adder_2_out), .out(multiplexer_3_out), .sel(and_1_out));
  Adder #(.width(32)) adder_2 (.a(adder_1_out), .b(shifter_1_out), .out(adder_2_out));  // open: cin, cout
  and and_1 (and_1_out, control_unit_circuit_1_branch, alu_32_1_zero_signal);
  Multiplexer #(.width(32), .enable("false")) multiplexer_4 (
    .in0(alu_32_1_aluresult), .in1(data_memory_1_data_read_from_memory), .out(multiplexer_4_out),
    .sel(control_unit_circuit_1_memtoreg));

  // Notes on the sheet:
  //   shift
  //   left 2
  //   branch
endmodule

module ALU_32 (
  input  [31:0] num1,
  input  [31:0] num2,
  input  [3:0] operation,
  output [31:0] ALUresult,
  output zero_signal,
  output overflow_bit,
  output underflow_bit
);

  wire comparator_1_lt;
  wire [31:0] adder_1_out, AND_out, bit_extender_1_out, OR_out, subtractor_1_out;

  assign AND_out = num1 & num2;  // AND_Gate AND, 32 bits wide
  assign OR_out = num1 | num2;  // OR_Gate OR, 32 bits wide
  Adder #(.width(32)) adder_1 (.a(num1), .b(num2), .out(adder_1_out));  // open: cin, cout
  Subtractor #(.width(32)) subtractor_1 (.a(num1), .b(num2), .out(subtractor_1_out));  // open: bin, bout
  Comparator #(.width(32)) comparator_1 (.a(num1), .b(num2), .lt(comparator_1_lt));  // open: gt, eq
  assign bit_extender_1_out = {{31{1'b0}}, comparator_1_lt};  // Bit_Extender bit_extender_1
  Multiplexer #(.select(4), .width(32), .enable("false")) multiplexer_1 (
    .in0(AND_out), .in1(OR_out), .in2(adder_1_out), .in6(subtractor_1_out), .in7(bit_extender_1_out),
    .out(ALUresult), .sel(operation));  // open: in3, in4, in5, in8, in9, in10, in11, in12, in13, in14, in15
  overflow overflow_1 (.in_1(num1), .in_2(num2), .in_3(adder_1_out), .out_4(overflow_bit));
  underflow underflow_1 (.in_1(num1), .in_2(num2), .in_3(subtractor_1_out), .out_4(underflow_bit));
  Comparator #(.width(32)) comparator_2 (.a(num1), .b(num2), .eq(zero_signal));  // open: gt, lt

  // Notes on the sheet:
  //   First 32 bit number
  //   Second 32 bit number
  //   0000
  //   0001
  //   0010
  //   ADD
  //   0110
  //   SUB
  //   0111
  //   SLT
  //   Zero signal
endmodule

module main_control_unit (
  input  [5:0] opcode,
  output aluop1,
  output aluop0
);

  wire not_1_out, not_2_out;

  not not_1 (not_1_out, opcode[3]);
  not not_2 (not_2_out, opcode[1]);
  and and_1 (aluop1, not_1_out, not_2_out);

  assign aluop0 = opcode[3];
endmodule

module aluop_funct_alucontrol (
  input  [1:0] ALUOp,
  input  [5:0] funct_bits,
  output [3:0] ALU_Control
);

  wire and_2_out, and_3_out, not_1_out, not_2_out;

  and and_1 (ALU_Control[2], ALUOp[1], funct_bits[1]);
  not not_1 (not_1_out, ALUOp[1]);
  not not_2 (not_2_out, funct_bits[2]);
  and and_2 (and_2_out, ALUOp[1], funct_bits[0]);
  and and_3 (and_3_out, ALUOp[1], funct_bits[3]);
  or or_1 (ALU_Control[1], not_1_out, not_2_out);
  or or_2 (ALU_Control[0], and_2_out, and_3_out);

  assign ALU_Control[3] = 1'b0;
endmodule

module overflow (
  input  [31:0] in_1,
  input  [31:0] in_2,
  input  [31:0] in_3,
  output out_4
);

  wire and_1_out, and_2_out, not_1_out, not_2_out, not_3_out;

  not not_1 (not_1_out, in_2[31]);
  not not_2 (not_2_out, in_3[31]);
  not not_3 (not_3_out, in_1[31]);
  and and_1 (and_1_out, in_1[31], in_2[31], not_2_out);
  and and_2 (and_2_out, not_3_out, not_1_out, in_3[31]);
  or or_1 (out_4, and_1_out, and_2_out);

  // Notes on the sheet:
  //   Overflow Detection
endmodule

module register_file (
  input  [31:0] WriteData,
  input  ControlPort,
  input  [4:0] regDest,
  input  [4:0] readReg1,
  input  [4:0] readReg2,
  output [31:0] readData1,
  output [31:0] readData2
);

  wire _0, _1, _2, _3, _4, _5, _6, _7, _8, _9, _10, _11, _12, _13, _14, _15, _16, _17, _18, _19, _20, _21,
       _22, _23, _24, _25, _26, _27, _28, _29, _30, _31, clock_1_out, clock_2_out, clock_3_out, clock_4_out,
       clock_5_out, clock_6_out, clock_7_out, clock_8_out, clock_9_out, clock_10_out, clock_11_out,
       clock_12_out, clock_13_out, clock_14_out, clock_15_out, clock_16_out, clock_17_out, clock_18_out,
       clock_19_out, clock_20_out, clock_21_out, clock_22_out, clock_23_out, clock_24_out, clock_25_out,
       clock_26_out, clock_27_out, clock_28_out, clock_29_out, clock_30_out, clock_31_out, clock_32_out;
  wire [31:0] _00, _01, _02, _03, _04, _05, _06, _07, _08, _09, _010, _011, _012, _013, _014, _015, _016,
       _017, _018, _019, _020, _021, _022, _023, _024, _025, _026, _027, _028, _029, _030, _031;

  Demultiplexer #(.select(5), .enable("false")) demultiplexer_1 (
    .out0(_0), .out1(_1), .out2(_2), .out3(_3), .out4(_4), .out5(_5), .out6(_6), .out7(_7), .out8(_8),
    .out9(_9), .out10(_10), .out11(_11), .out12(_12), .out13(_13), .out14(_14), .out15(_15), .out16(_16),
    .out17(_17), .out18(_18), .out19(_19), .out20(_20), .out21(_21), .out22(_22), .out23(_23), .out24(_24),
    .out25(_25), .out26(_26), .out27(_27), .out28(_28), .out29(_29), .out30(_30), .out31(_31),
    .in(ControlPort), .sel(regDest));
  Register #(.width(32)) register_1 (.D(WriteData), .en(_1), .Q(_01), .clk(clock_1_out));  // open: clr
  Clock clock_1 (.out(clock_1_out));
  Register #(.width(32)) u__2 (.D(WriteData), .en(_2), .Q(_02), .clk(clock_2_out));  // open: clr
  Clock clock_2 (.out(clock_2_out));
  Register #(.width(32)) register_2 (.D(WriteData), .en(_3), .Q(_03), .clk(clock_3_out));  // open: clr
  Clock clock_3 (.out(clock_3_out));
  Register #(.width(32)) register_3 (.D(WriteData), .en(_4), .Q(_04), .clk(clock_4_out));  // open: clr
  Clock clock_4 (.out(clock_4_out));
  Clock clock_5 (.out(clock_5_out));
  Clock clock_6 (.out(clock_6_out));
  Clock clock_7 (.out(clock_7_out));
  Clock clock_8 (.out(clock_8_out));
  Clock clock_9 (.out(clock_9_out));
  Clock clock_10 (.out(clock_10_out));
  Clock clock_11 (.out(clock_11_out));
  Clock clock_12 (.out(clock_12_out));
  Clock clock_13 (.out(clock_13_out));
  Clock clock_14 (.out(clock_14_out));
  Clock clock_15 (.out(clock_15_out));
  Clock clock_16 (.out(clock_16_out));
  Clock clock_17 (.out(clock_17_out));
  Clock clock_18 (.out(clock_18_out));
  Clock clock_19 (.out(clock_19_out));
  Clock clock_20 (.out(clock_20_out));
  Clock clock_21 (.out(clock_21_out));
  Clock clock_22 (.out(clock_22_out));
  Clock clock_23 (.out(clock_23_out));
  Clock clock_24 (.out(clock_24_out));
  Clock clock_25 (.out(clock_25_out));
  Clock clock_26 (.out(clock_26_out));
  Clock clock_27 (.out(clock_27_out));
  Clock clock_28 (.out(clock_28_out));
  Clock clock_29 (.out(clock_29_out));
  Clock clock_30 (.out(clock_30_out));
  Clock clock_31 (.out(clock_31_out));
  Register #(.width(32)) register_4 (.D(WriteData), .en(_5), .Q(_05), .clk(clock_5_out));  // open: clr
  Register #(.width(32)) register_5 (.D(WriteData), .en(_6), .Q(_06), .clk(clock_6_out));  // open: clr
  Register #(.width(32)) register_6 (.D(WriteData), .en(_7), .Q(_07), .clk(clock_7_out));  // open: clr
  Register #(.width(32)) u__8 (.D(WriteData), .en(_8), .Q(_08), .clk(clock_8_out));  // open: clr
  Register #(.width(32)) register_7 (.D(WriteData), .en(_9), .Q(_09), .clk(clock_9_out));  // open: clr
  Register #(.width(32)) register_8 (.D(WriteData), .en(_10), .Q(_010), .clk(clock_10_out));  // open: clr
  Register #(.width(32)) register_9 (.D(WriteData), .en(_11), .Q(_011), .clk(clock_11_out));  // open: clr
  Register #(.width(32)) register_10 (.D(WriteData), .en(_12), .Q(_012), .clk(clock_12_out));  // open: clr
  Register #(.width(32)) u__13 (.D(WriteData), .en(_13), .Q(_013), .clk(clock_13_out));  // open: clr
  Register #(.width(32)) register_11 (.D(WriteData), .en(_14), .Q(_014), .clk(clock_14_out));  // open: clr
  Register #(.width(32)) register_12 (.D(WriteData), .en(_15), .Q(_015), .clk(clock_15_out));  // open: clr
  Register #(.width(32)) register_13 (.D(WriteData), .en(_16), .Q(_016), .clk(clock_16_out));  // open: clr
  Register #(.width(32)) register_14 (.D(WriteData), .en(_17), .Q(_017), .clk(clock_17_out));  // open: clr
  Register #(.width(32)) u__18 (.D(WriteData), .en(_18), .Q(_018), .clk(clock_18_out));  // open: clr
  Register #(.width(32)) register_15 (.D(WriteData), .en(_19), .Q(_019), .clk(clock_19_out));  // open: clr
  Register #(.width(32)) register_16 (.D(WriteData), .en(_20), .Q(_020), .clk(clock_20_out));  // open: clr
  Register #(.width(32)) register_17 (.D(WriteData), .en(_21), .Q(_021), .clk(clock_21_out));  // open: clr
  Register #(.width(32)) register_18 (.D(WriteData), .en(_22), .Q(_022), .clk(clock_22_out));  // open: clr
  Register #(.width(32)) u__23 (.D(WriteData), .en(_23), .Q(_023), .clk(clock_23_out));  // open: clr
  Register #(.width(32)) register_19 (.D(WriteData), .en(_24), .Q(_024), .clk(clock_24_out));  // open: clr
  Register #(.width(32)) register_20 (.D(WriteData), .en(_25), .Q(_025), .clk(clock_25_out));  // open: clr
  Register #(.width(32)) register_21 (.D(WriteData), .en(_26), .Q(_026), .clk(clock_26_out));  // open: clr
  Register #(.width(32)) register_22 (.D(WriteData), .en(_27), .Q(_027), .clk(clock_27_out));  // open: clr
  Register #(.width(32)) u__28 (.D(WriteData), .en(_28), .Q(_028), .clk(clock_28_out));  // open: clr
  Register #(.width(32)) register_23 (.D(WriteData), .en(_29), .Q(_029), .clk(clock_29_out));  // open: clr
  Register #(.width(32)) register_24 (.D(WriteData), .en(_30), .Q(_030), .clk(clock_30_out));  // open: clr
  Register #(.width(32)) register_25 (.D(WriteData), .en(_31), .Q(_031), .clk(clock_31_out));  // open: clr
  Register #(.width(32)) register_26 (.en(_0), .Q(_00), .clk(clock_32_out));  // open: D, clr
  Clock clock_32 (.out(clock_32_out));
  Multiplexer #(.select(5), .width(32), .enable("false")) multiplexer_1 (
    .in0(_00), .in1(_01), .in2(_02), .in3(_03), .in4(_04), .in5(_05), .in6(_06), .in7(_07), .in8(_08),
    .in9(_09), .in10(_010), .in11(_011), .in12(_012), .in13(_013), .in14(_014), .in15(_015), .in16(_016),
    .in17(_017), .in18(_018), .in19(_019), .in20(_020), .in21(_021), .in22(_022), .in23(_023), .in24(_024),
    .in25(_025), .in26(_026), .in27(_027), .in28(_028), .in29(_029), .in30(_030), .in31(_031),
    .out(readData1), .sel(readReg1));
  Multiplexer #(.select(5), .width(32), .enable("false")) multiplexer_2 (
    .in0(_00), .in1(_01), .in2(_02), .in3(_03), .in4(_04), .in5(_05), .in6(_06), .in7(_07), .in8(_08),
    .in9(_09), .in10(_010), .in11(_011), .in12(_012), .in13(_013), .in14(_014), .in15(_015), .in16(_016),
    .in17(_017), .in18(_018), .in19(_019), .in20(_020), .in21(_021), .in22(_022), .in23(_023), .in24(_024),
    .in25(_025), .in26(_026), .in27(_027), .in28(_028), .in29(_029), .in30(_030), .in31(_031),
    .out(readData2), .sel(readReg2));

  // Notes on the sheet:
  //   register on which data has to be written
  //   write this data onto a register
  //   1
  //   3
  //   4
  //   5
  //   6
  //   7
  //   9
  //   10
  //   11
  //   12
  //   14
  //   15
  //   16
  //   17
  //   19
  //   20
  //   21
  //   22
  //   24
  //   25
  //   26
  //   27
  //   29
  //   30
  //   31
  //   0
  //   register from which data has to be read
  //   register from which data has to be read
  //   read data from selected register number
  //   read data from selected register number
endmodule

module underflow (
  input  [31:0] in_1,
  input  [31:0] in_2,
  input  [31:0] in_3,
  output out_4
);

  wire xor_1_out, xor_2_out;

  xor xor_1 (xor_1_out, in_1[31], in_2[31]);
  xor xor_2 (xor_2_out, in_1[31], in_3[31]);
  and and_1 (out_4, xor_1_out, xor_2_out);

  // Notes on the sheet:
  //   Underflow detection
endmodule

module control_unit (
  input  op5,
  input  op4,
  input  op3,
  input  op2,
  input  op1,
  input  op0,
  output regDest,
  output jump,
  output branch,
  output memRead,
  output memToReg,
  output ALUOp1,
  output ALUOp0,
  output memWrite,
  output ALUSrc,
  output regWrite
);

  wire and_1_out, and_2_out, and_3_out, and_4_out, and_5_out, and_6_out, and_7_out, and_8_out, and_9_out,
       and_10_out, and_11_out, and_12_out, and_13_out, and_14_out, and_15_out, and_16_out, and_18_out,
       and_19_out, and_20_out, and_21_out, and_22_out, and_23_out, and_24_out, and_25_out, and_26_out,
       and_27_out, and_28_out, and_29_out, and_30_out, and_31_out, and_33_out, and_34_out, and_35_out,
       and_36_out, and_37_out, and_38_out, and_39_out, and_40_out, and_41_out, and_42_out, not_1_out,
       not_2_out, not_3_out, not_4_out, not_5_out, not_6_out, not_7_out, not_8_out, not_9_out, not_10_out,
       not_11_out, not_12_out, not_13_out, not_14_out, not_15_out, not_16_out, not_17_out, not_18_out,
       not_19_out, not_20_out, not_21_out, not_22_out, not_23_out, not_24_out, not_25_out, not_26_out,
       not_27_out, not_28_out, not_29_out, not_30_out, not_31_out, not_32_out, not_33_out, not_34_out,
       not_35_out, not_36_out, not_37_out, not_38_out, not_39_out, not_40_out, not_41_out, not_42_out,
       not_43_out, not_44_out, not_45_out, not_46_out, not_47_out, not_48_out, not_49_out, not_50_out,
       not_51_out, not_52_out, not_53_out, not_54_out, not_55_out, not_56_out, not_57_out, not_58_out,
       not_59_out, not_60_out, not_61_out, not_62_out, not_63_out, not_64_out, not_65_out, not_66_out,
       not_67_out, not_68_out, not_69_out, not_70_out, not_71_out, not_72_out;

  not not_1 (not_1_out, op3);
  not not_2 (not_2_out, op2);
  not not_3 (not_3_out, op1);
  not not_4 (not_4_out, op5);
  not not_5 (not_5_out, op2);
  not not_6 (not_6_out, op2);
  not not_7 (not_7_out, op0);
  not not_8 (not_8_out, op2);
  not not_9 (not_9_out, op2);
  not not_10 (not_10_out, op1);
  not not_11 (not_11_out, op5);
  not not_12 (not_12_out, op0);
  not not_13 (not_13_out, op1);
  not not_14 (not_14_out, op5);
  not not_15 (not_15_out, op4);
  not not_16 (not_16_out, op1);
  not not_17 (not_17_out, op0);
  not not_18 (not_18_out, op5);
  not not_19 (not_19_out, op0);
  not not_20 (not_20_out, op1);
  not not_21 (not_21_out, op4);
  not not_22 (not_22_out, op3);
  not not_23 (not_23_out, op2);
  not not_24 (not_24_out, op5);
  not not_25 (not_25_out, op4);
  not not_26 (not_26_out, op3);
  not not_27 (not_27_out, op2);
  not not_28 (not_28_out, op0);
  not not_29 (not_29_out, op5);
  not not_30 (not_30_out, op4);
  not not_31 (not_31_out, op3);
  not not_32 (not_32_out, op1);
  not not_33 (not_33_out, op0);
  not not_34 (not_34_out, op4);
  not not_35 (not_35_out, op2);
  not not_36 (not_36_out, op5);
  not not_37 (not_37_out, op3);
  not not_38 (not_38_out, op2);
  not not_39 (not_39_out, op3);
  not not_40 (not_40_out, op2);
  not not_41 (not_41_out, op1);
  not not_42 (not_42_out, op3);
  not not_43 (not_43_out, op2);
  not not_44 (not_44_out, op0);
  not not_45 (not_45_out, op3);
  not not_46 (not_46_out, op2);
  not not_47 (not_47_out, op5);
  not not_48 (not_48_out, op4);
  not not_49 (not_49_out, op2);
  not not_50 (not_50_out, op0);
  not not_51 (not_51_out, op5);
  not not_52 (not_52_out, op4);
  not not_53 (not_53_out, op1);
  not not_54 (not_54_out, op0);
  not not_55 (not_55_out, op5);
  not not_56 (not_56_out, op1);
  not not_57 (not_57_out, op0);
  not not_58 (not_58_out, op4);
  not not_59 (not_59_out, op2);
  not not_60 (not_60_out, op5);
  not not_61 (not_61_out, op4);
  not not_62 (not_62_out, op0);
  not not_63 (not_63_out, op4);
  not not_64 (not_64_out, op5);
  not not_65 (not_65_out, op4);
  not not_66 (not_66_out, op2);
  not not_67 (not_67_out, op1);
  not not_68 (not_68_out, op0);
  not not_69 (not_69_out, op3);
  not not_70 (not_70_out, op3);
  not not_71 (not_71_out, op3);
  not not_72 (not_72_out, op3);
  and and_1 (and_1_out, not_1_out, not_2_out, not_3_out);
  and and_2 (and_2_out, not_4_out, not_5_out, op0);
  and and_3 (and_3_out, not_6_out, op1, not_7_out);
  and and_4 (and_4_out, op4, not_8_out);
  and and_5 (and_5_out, op5, not_9_out, not_10_out);
  and and_6 (and_6_out, not_11_out, op0);
  and and_7 (and_7_out, op1, not_12_out);
  and and_8 (and_8_out, op3, op2);
  and and_9 (and_9_out, op5, not_13_out);
  and and_10 (and_10_out, op5, op2);
  and and_11 (and_11_out, not_14_out, not_15_out, op2, not_16_out, not_17_out);
  and and_12 (and_12_out, not_18_out, op3, op0);
  and and_13 (and_13_out, op3, op1, not_19_out);
  and and_14 (and_14_out, op3, op2);
  and and_15 (and_15_out, op4, op3);
  and and_16 (and_16_out, op5, op3, not_20_out);
  and and_17 (memRead, op5, not_21_out, not_22_out, not_23_out, op1, op0);
  and and_18 (and_18_out, not_24_out, not_25_out, not_26_out, not_27_out, op1, not_28_out);
  and and_19 (and_19_out, not_29_out, not_30_out, not_31_out, op2, not_32_out, not_33_out);
  and and_20 (and_20_out, op5, not_34_out, not_35_out, op1, op0);
  and and_21 (and_21_out, not_36_out, not_37_out, not_38_out);
  and and_22 (and_22_out, not_39_out, not_40_out, not_41_out);
  and and_23 (and_23_out, not_42_out, not_43_out, not_44_out);
  and and_24 (and_24_out, op4, not_45_out, not_46_out);
  and and_25 (and_25_out, not_47_out, not_48_out, not_49_out, op1, not_50_out);
  and and_26 (and_26_out, not_51_out, not_52_out, op2, not_53_out, not_54_out);
  and and_27 (and_27_out, not_55_out, op3, op0);
  and and_28 (and_28_out, op3, op2);
  and and_29 (and_29_out, op4, op3);
  and and_30 (and_30_out, op5, op3, not_56_out);
  and and_31 (and_31_out, op5, op3, not_57_out);
  and and_32 (memWrite, op5, not_58_out, op3, not_59_out, op1, op0);
  and and_33 (and_33_out, not_60_out, not_61_out, op1, not_62_out);
  and and_34 (and_34_out, op2, op0);
  and and_35 (and_35_out, op4, op2);
  and and_36 (and_36_out, op5, not_63_out, op1, op0);
  and and_37 (and_37_out, op5, op2);
  and and_38 (and_38_out, not_64_out, not_65_out, not_66_out, not_67_out, not_68_out);
  and and_39 (and_39_out, not_69_out, op0);
  and and_40 (and_40_out, not_70_out, op2, op1);
  and and_41 (and_41_out, op4, not_71_out);
  and and_42 (and_42_out, op5, not_72_out);
  or or_1 (regDest, and_1_out, and_2_out, and_3_out, and_4_out, and_5_out);
  or or_2 (jump, and_6_out, and_7_out, and_8_out, op4, and_9_out, and_10_out);
  or or_3 (branch, and_11_out, and_12_out, and_13_out, and_14_out, and_15_out, and_16_out);
  or or_4 (memToReg, and_18_out, and_19_out, and_20_out);
  or or_5 (ALUOp1, and_21_out, and_22_out, and_23_out, and_24_out);
  or or_6 (ALUOp0, and_25_out, and_26_out, and_27_out, and_28_out, and_29_out, and_30_out, and_31_out);
  or or_7 (ALUSrc, and_33_out, and_34_out, op3, and_35_out, and_36_out, and_37_out);
  or or_8 (regWrite, and_38_out, and_39_out, and_40_out, and_41_out, and_42_out);
endmodule

module control_unit_circuit (
  input  [5:0] opcode,
  output regDest,
  output jump,
  output branch,
  output memRead,
  output memToReg,
  output [1:0] ALUOp,
  output memWrite,
  output ALUSrc,
  output regWrite
);

  control_unit control_unit_1 (
    .op5(opcode[5]), .op4(opcode[4]), .op3(opcode[3]), .op2(opcode[2]), .op1(opcode[1]), .op0(opcode[0]),
    .regDest(regDest), .jump(jump), .branch(branch), .memRead(memRead), .memToReg(memToReg),
    .ALUOp1(ALUOp[1]), .ALUOp0(ALUOp[0]), .memWrite(memWrite), .ALUSrc(ALUSrc), .regWrite(regWrite));

  // Notes on the sheet:
  //   ALUOp1
  //   ALUOp0
endmodule

module instruction_memory (
  input  [31:0] address_of_instruction,
  output [31:0] instruction_itself
);

  wire clock_1_out;
  wire [23:0] bit_extender_1_out;

  Bit_Extender #(.in_width(32), .out_width(24)) bit_extender_1 (.in(address_of_instruction), .out(bit_extender_1_out));
  Clock clock_1 (.out(clock_1_out));
  ROM #(.addrWidth(24), .dataWidth(32)) rom_1 (.addr(bit_extender_1_out), .data(instruction_itself));  // open: sel

  // Notes on the sheet:
  //   contents of rom_1 (hex, n*v repeats v):
  //   20080000 0 0 0 20090003 0 0 0 200a0001 0 0 0 3c010000 0 0 0 3421aaaa 0 0 0 18020 0 0 0 3c010000 0 0
  //   0 3421f0f0 0 0 0 18820 0 0 0 11090004 0 0 0 2288825 0 0 0 2089024 0 0 0 10a4020 0 0 0 1000fffb
endmodule

module data_memory (
  input  [31:0] memory_address,
  input  in_2,
  input  in_3,
  input  [31:0] data_to_be_written,
  output [31:0] data_read_from_memory
);

  wire clock_1_out;
  wire [23:0] bit_extender_1_out;

  Bit_Extender #(.in_width(32), .out_width(24)) bit_extender_1 (.in(memory_address), .out(bit_extender_1_out));
  Clock clock_1 (.out(clock_1_out));
  RAM #(.addrWidth(24), .dataWidth(32), .bus("separate")) ram_1 (
    .addr(bit_extender_1_out), .din(data_to_be_written), .data(data_read_from_memory), .str(in_2),
    .clk(clock_1_out), .ld(in_3));  // open: sel, clr
endmodule
